// Logisim project alu.circ as structural Verilog: 1 circuit, main circuit alu
module alu (
  input  [31:0] A,
  input  [31:0] B,
  input  [3:0] ALUSel,
  output [31:0] Result
);

  wire comparator_2_gt, comparator_3_lt, xor_2_out;
  wire [0:0] slt_cfe5b6cd;
  wire [31:0] add, and_5d5e71c2, div_44c3e5f8, mulh_366169a8, mult_c0ca873f, multiplexer_1_out,
       multiplexer_2_out, multiplier_2_cout, or_d2719426, rem_47eb8f05, sll_8a914702, sra_7e603141,
       srl_c2f3df62, sub_3d5478aa, subtractor_2_out, subtractor_3_out, subtractor_4_out, xor_3ec28554;

  Adder #(.width(32)) adder_1 (.a(A), .b(B), .out(add));  // open: cin, cout
  assign and_5d5e71c2 = A & B;  // AND_Gate and_1, 32 bits wide
  assign or_d2719426 = A | B;  // OR_Gate or_1, 32 bits wide
  assign xor_3ec28554 = A ^ B;  // XOR_Gate xor_1, 32 bits wide
  Shifter #(.width(32), .shift("lr")) shifter_1 (.in(A), .\dist (B[4:0]), .out(srl_c2f3df62));
  Shifter #(.width(32), .shift("ar")) shifter_2 (.in(A), .\dist (B[4:0]), .out(sra_7e603141));
  Shifter #(.width(32)) shifter_3 (.in(A), .\dist (B[4:0]), .out(sll_8a914702));
  Comparator #(.width(32)) comparator_1 (.a(A), .b(B), .lt(slt_cfe5b6cd[0]));  // open: gt, eq
  Divider #(.width(32)) divider_1 (.a(A), .b(B), .out(div_44c3e5f8), .rem(rem_47eb8f05));  // open: upper
  Multiplier #(.width(32)) multiplier_1 (.a(A), .b(B), .out(mult_c0ca873f));  // open: cin, cout
  Subtractor #(.width(32)) subtractor_1 (.a(A), .b(B), .out(sub_3d5478aa));  // open: bin, bout
  Comparator #(.width(32)) comparator_2 (.a({32{1'b0}}), .b(A), .gt(comparator_2_gt));  // open: eq, lt
  Subtractor #(.width(32)) subtractor_2 (.a({32{1'b0}}), .b(A), .out(subtractor_2_out));  // open: bin, bout
  Subtractor #(.width(32)) subtractor_3 (.a({32{1'b0}}), .b(B), .out(subtractor_3_out));  // open: bin, bout
  Comparator #(.width(32)) comparator_3 (.a(B), .b({32{1'b0}}), .lt(comparator_3_lt));  // open: gt, eq
  Multiplexer #(.width(32), .enable("false")) multiplexer_1 (
    .in0(A), .in1(subtractor_2_out), .out(multiplexer_1_out), .sel(comparator_2_gt));
  Multiplexer #(.width(32), .enable("false")) multiplexer_2 (
    .in0(B), .in1(subtractor_3_out), .out(multiplexer_2_out), .sel(comparator_3_lt));
  Multiplier #(.width(32)) multiplier_2 (
    .a(multiplexer_1_out), .b(multiplexer_2_out), .cout(multiplier_2_cout));  // open: out, cin
  Multiplexer #(.select(4), .width(32), .enable("false")) multiplexer_3 (
    .in0(add), .in1(and_5d5e71c2), .in2(or_d2719426), .in3(xor_3ec28554), .in4(srl_c2f3df62),
    .in5(sra_7e603141), .in6(sll_8a914702), .in7({{31{1'b0}}, slt_cfe5b6cd[0]}), .in8(div_44c3e5f8),
    .in9(rem_47eb8f05), .in10(mult_c0ca873f), .in11(mulh_366169a8), .in12(sub_3d5478aa), .in13(B),
    .out(Result), .sel(ALUSel));  // open: in14, in15
  Subtractor #(.width(32)) subtractor_4 (
    .a({32{1'b1}}), .b(multiplier_2_cout), .out(subtractor_4_out));  // open: bin, bout
  xor xor_2 (xor_2_out, comparator_2_gt, comparator_3_lt);
  Multiplexer #(.width(32), .enable("false")) multiplexer_4 (
    .in0(multiplier_2_cout), .in1(subtractor_4_out), .out(mulh_366169a8), .sel(xor_2_out));

  // Notes on the sheet:
  //   INPUTS to your circuit
  //   DON'T CHANGE THE LOCATIONS OF THE INPUTS AND OUTPUTS!
  //   OUTPUT from your circuit
endmodule
