// Logisim project cpu.circ as structural Verilog: 4 circuits, main circuit branch_cp
module main (
  input  [31:0] INSTRUCTION,
  input  CLOCK,
  output [31:0] FETCH_ADDRESS,
  output [31:0] ra,
  output [31:0] sp,
  output [31:0] t0,
  output [31:0] t1,
  output [31:0] t2,
  output [31:0] s0,
  output [31:0] s1,
  output [31:0] a0
);

  wire ASel, BrEq, BrLt, BrUn, BSel, MemW, PCSel, RegWEn, rem_2;
  wire [1:0] MemLnth, rem_4, WBSel;
  wire [2:0] ImmSel;
  wire [3:0] ALUSel;
  wire [7:0] multiplexer_5_out;
  wire [15:0] MEM_p5, MEM_p5_2, multiplexer_6_out;
  wire [31:0] adder_1_out, alu_922a7f15, bit_extender_1_out, bit_extender_2_out, divider_2_out, im,
       main_1_read_data_1, main_1_read_data_2, multiplexer_1_out, multiplexer_2_out, multiplexer_3_out,
       multiplexer_4_out, multiplexer_7_out, pc, pc_4_afterclock, register_1_q, shifter_1_out, wr_b;
  wire [31:1] divider_3_rem;
  wire [31:2] divider_1_rem;

  Multiplexer #(.width(32), .enable("false")) multiplexer_1 (
    .in0(INSTRUCTION), .in1({32{1'b0}}), .out(multiplexer_1_out), .sel(PCSel));
  Register #(.width(32)) register_1 (.D(multiplexer_1_out), .clk(CLOCK), .Q(register_1_q));  // open: en, clr
  ImmGen immgen_1 (.instr(register_1_q), .ImmSel(ImmSel), .imm_32(im));
  control control_1 (
    .instr(register_1_q), .BrEq(BrEq), .BrLt(BrLt), .ImmSel(ImmSel), .RegWEn(RegWEn), .ASel(ASel),
    .BSel(BSel), .ALUSel(ALUSel), .MemW(MemW), .WBSel(WBSel), .PCSel(PCSel), .BrUn(BrUn), .MemLnth(MemLnth));
  branch_cp branch_cp_1 (
    .equal(BrEq), .signed_0(BrUn), .R1(main_1_read_data_1), .lessthan(BrLt), .R2(main_1_read_data_2));
  regfile_main main_1 (
    .Read_Register_1_rs1(register_1_q[19:15]), .Read_Register_2_rs2(register_1_q[24:20]),
    .Write_Register_rd(register_1_q[11:7]), .Write_Data(wr_b), .Write_Enable(RegWEn), .Clock(CLOCK),
    .Read_Data_1(main_1_read_data_1), .Read_Data_2(main_1_read_data_2), .ra(ra), .sp(sp), .t0(t0), .t1(t1),
    .t2(t2), .s0(s0), .s1(s1), .a0(a0));
  Multiplexer #(.width(32), .enable("false")) multiplexer_2 (
    .in0(main_1_read_data_2), .in1(im), .out(multiplexer_2_out), .sel(BSel));
  Multiplexer #(.width(32), .enable("false")) multiplexer_3 (
    .in0(main_1_read_data_1), .in1(pc), .out(multiplexer_3_out), .sel(ASel));
  alu alu_1 (.Result(alu_922a7f15), .ALUSel(ALUSel), .B(multiplexer_2_out), .A(multiplexer_3_out));
  Divider #(.width(32)) divider_1 (.a(alu_922a7f15), .b(32'h4), .rem({divider_1_rem, rem_4}));  // open: out, upper
  Adder #(.width(32)) adder_1 (.a(pc_4_afterclock), .b(32'h4), .out(adder_1_out));  // open: cin, cout
  Register #(.width(32)) u_PC (.D(multiplexer_4_out), .clk(CLOCK), .Q(pc_4_afterclock));  // open: en, clr
  Multiplexer #(.width(32), .enable("false")) multiplexer_4 (
    .in0(adder_1_out), .in1(alu_922a7f15), .out(multiplexer_4_out), .sel(PCSel));
  Shifter #(.width(32), .shift("ar")) shifter_1 (.in(alu_922a7f15), .\dist (5'b00010), .out(shifter_1_out));
  // mem_main MEM: pin names not known; wires that end beside it: shifter_1_out, main_1_read_data_2, MemW, CLOCK, {MEM_p5_2, MEM_p5}
  Divider #(.width(32)) divider_2 (.a(alu_922a7f15), .b(32'h2), .out(divider_2_out));  // open: upper, rem
  Divider #(.width(32)) divider_3 (.a(divider_2_out), .b(32'h2), .rem({divider_3_rem, rem_2}));  // open: out, upper
  Register #(.width(32)) register_2 (.D(pc_4_afterclock), .clk(CLOCK), .Q(pc));  // open: en, clr
  Shifter #(.width(32), .shift("ar")) shifter_2 (.in(pc_4_afterclock), .\dist (5'b00010), .out(FETCH_ADDRESS));
  Multiplexer #(.select(2), .width(8), .enable("false")) multiplexer_5 (
    .in0(MEM_p5[7:0]), .in1(MEM_p5[15:8]), .in2(MEM_p5_2[7:0]), .in3(MEM_p5_2[15:8]),
    .out(multiplexer_5_out), .sel(rem_4));
  Multiplexer #(.width(16), .enable("false")) multiplexer_6 (
    .in0(MEM_p5), .in1(MEM_p5_2), .out(multiplexer_6_out), .sel(rem_2));
  assign bit_extender_1_out = {{24{multiplexer_5_out[7]}}, multiplexer_5_out};  // Bit_Extender bit_extender_1
  assign bit_extender_2_out = {{16{multiplexer_6_out[15]}}, multiplexer_6_out};  // Bit_Extender bit_extender_2
  Multiplexer #(.select(2), .width(32), .enable("false")) multiplexer_7 (
    .in0(bit_extender_1_out), .in1(bit_extender_2_out), .in2({MEM_p5_2, MEM_p5}), .out(multiplexer_7_out),
    .sel(MemLnth));  // open: in3
  Multiplexer #(.select(2), .width(32), .enable("false")) multiplexer_8 (
    .in0(multiplexer_7_out), .in1(alu_922a7f15), .in2(pc_4_afterclock), .out(wr_b), .sel(WBSel));  // open: in3

  // Other names for the same wires on the sheet: a0_135d104d[31:0] = a0; clk = CLOCK;
  //   fetch_addr[31:0] = FETCH_ADDRESS; ra_090d200a[31:0] = ra; s0_42308184[31:0] = s0; s1_e358774f[31:0] = s1;
  //   sp_a77b7c50[31:0] = sp; t0_7f286ada[31:0] = t0; t1_1ee51759[31:0] = t1; t2_d8aaf36b[31:0] = t2

  // Notes on the sheet:
  //   Output
  //   Inputs/Outputs from run.circ. DO NOT MOVE THESE.
  //   Inputs
  //   Inputs/Outputs from run.circ. DO NOT MOVE THESE.
  //   load word/ load half word/ load byte
  //   load word/ load half word/ load byte
endmodule

module branch_cp (
  input  [31:0] R1,
  input  [31:0] R2,
  input  signed_0,
  output equal,
  output lessthan
);

  wire comparator_1_lt, comparator_2_lt;

  Comparator #(.width(32)) comparator_1 (.a(R1), .b(R2), .eq(equal), .lt(comparator_1_lt));  // open: gt
  Comparator #(.width(32), .mode("unsigned")) comparator_2 (.a(R1), .b(R2), .lt(comparator_2_lt));  // open: gt, eq
  Multiplexer #(.enable("false")) multiplexer_1 (
    .in0(comparator_1_lt), .in1(comparator_2_lt), .out(lessthan), .sel(signed_0));
endmodule

module control (
  input  [31:0] instr,
  input  BrEq,
  input  BrLt,
  output [2:0] ImmSel,
  output RegWEn,
  output ASel,
  output BSel,
  output [3:0] ALUSel,
  output MemW,
  output [1:0] WBSel,
  output PCSel,
  output BrUn,
  output [1:0] MemLnth
);

  wire and_1_out, and_2_out, and_3_out, and_4_out, and_5_out, and_6_out, and_7_out, and_8_out, and_9_out,
       and_13_out, and_14_out, and_15_out, and_16_out, and_17_out, and_18_out, and_19_out, and_20_out,
       and_21_out, and_22_out, B, f3_0, f3_1, f3_2, f3_4, f3_5, f3_6, f3_7, f7_00, f7_01, f7_20, I_addi_out,
       I_andi_out, I_im, I_jalr, I_load, I_ori_out, I_xori_out, is_imm_PC, J, not_1_out, not_2_out,
       not_3_out, not_4_out, not_5_out, not_6_out, not_7_out, not_8_out, not_9_out, not_10_out, not_11_out,
       not_12_out, not_13_out, not_14_out, not_15_out, not_16_out, not_17_out, not_18_out, not_19_out,
       not_20_out, not_21_out, not_22_out, not_23_out, not_24_out, not_25_out, not_26_out, not_27_out,
       not_28_out, not_29_out, not_30_out, not_31_out, not_32_out, not_33_out, not_34_out, not_35_out,
       not_36_out, not_37_out, not_38_out, not_39_out, not_40_out, not_41_out, not_42_out, not_43_out,
       not_44_out, not_45_out, not_46_out, not_47_out, not_48_out, not_49_out, not_50_out, not_51_out,
       not_52_out, not_53_out, not_54_out, not_55_out, not_56_out, not_57_out, or_3_out, or_4_out, or_5_out,
       or_6_out, or_7_out, or_8_out, or_9_out, or_10_out, or_11_out, R, R_add_out, R_and_out, R_div_out,
       R_mult_out, R_multh_out, R_or_out, R_rem_out, R_sub_out, R_xor_out, sari_out, sll_slli_out,
       slt_slti_out, srl_srli_out, U;

  or or_1 (PCSel, and_1_out, and_2_out, and_3_out, and_4_out, J, I_jalr);
  not not_1 (not_1_out, instr[2]);
  not not_2 (not_2_out, instr[3]);
  not not_3 (not_3_out, instr[6]);
  not not_4 (not_4_out, instr[2]);
  not not_5 (not_5_out, instr[3]);
  not not_6 (not_6_out, instr[4]);
  not not_7 (not_7_out, instr[5]);
  not not_8 (not_8_out, instr[6]);
  not not_9 (not_9_out, instr[2]);
  not not_10 (not_10_out, instr[3]);
  not not_11 (not_11_out, instr[5]);
  not not_12 (not_12_out, instr[6]);
  not not_13 (not_13_out, instr[2]);
  not not_14 (not_14_out, instr[3]);
  not not_15 (not_15_out, instr[4]);
  not not_16 (not_16_out, instr[6]);
  not not_17 (not_17_out, instr[2]);
  not not_18 (not_18_out, instr[3]);
  not not_19 (not_19_out, instr[4]);
  not not_20 (not_20_out, instr[3]);
  not not_21 (not_21_out, instr[6]);
  not not_22 (not_22_out, instr[4]);
  not not_23 (not_23_out, instr[3]);
  not not_24 (not_24_out, instr[4]);
  and and_1 (and_1_out, and_5_out, BrEq);
  and and_2 (and_2_out, and_6_out, not_25_out);
  and and_3 (and_3_out, and_7_out, BrLt);
  and and_4 (and_4_out, and_8_out, BrLt);
  or or_2 (is_imm_PC, I_jalr, J, B, I_load, MemW);
  and hex33 (R, instr[0], instr[1], not_1_out, not_2_out, instr[4], instr[5], not_3_out);
  and hex03 (I_load, instr[0], instr[1], not_4_out, not_5_out, not_6_out, not_7_out, not_8_out);
  and hex13 (I_im, instr[0], instr[1], not_9_out, not_10_out, instr[4], not_11_out, not_12_out);
  and hex23 (MemW, instr[0], instr[1], not_13_out, not_14_out, not_15_out, instr[5], not_16_out);
  and hex63 (B, instr[0], instr[1], not_17_out, not_18_out, not_19_out, instr[5], instr[6]);
  and hex37 (U, instr[0], instr[1], instr[2], not_20_out, instr[4], instr[5], not_21_out);
  and hex6f (J, instr[0], instr[1], instr[2], instr[3], not_22_out, instr[5], instr[6]);
  and hex67 (I_jalr, instr[0], instr[1], instr[2], not_23_out, not_24_out, instr[5], instr[6]);
  and and_5 (and_5_out, B, f3_0);
  and and_6 (and_6_out, B, f3_1);
  not not_25 (not_25_out, BrEq);
  and and_7 (and_7_out, B, f3_6);
  and and_8 (and_8_out, B, f3_4);
  not not_26 (not_26_out, instr[12]);
  not not_27 (not_27_out, instr[13]);
  not not_28 (not_28_out, instr[14]);
  not not_29 (not_29_out, instr[13]);
  not not_30 (not_30_out, instr[14]);
  not not_31 (not_31_out, instr[12]);
  not not_32 (not_32_out, instr[14]);
  not not_33 (not_33_out, instr[12]);
  not not_34 (not_34_out, instr[13]);
  not not_35 (not_35_out, instr[13]);
  not not_36 (not_36_out, instr[12]);
  not not_37 (not_37_out, instr[25]);
  not not_38 (not_38_out, instr[26]);
  not not_39 (not_39_out, instr[27]);
  not not_40 (not_40_out, instr[28]);
  not not_41 (not_41_out, instr[29]);
  not not_42 (not_42_out, instr[30]);
  not not_43 (not_43_out, instr[31]);
  not not_44 (not_44_out, instr[26]);
  not not_45 (not_45_out, instr[27]);
  not not_46 (not_46_out, instr[28]);
  not not_47 (not_47_out, instr[29]);
  not not_48 (not_48_out, instr[30]);
  not not_49 (not_49_out, instr[31]);
  not not_50 (not_50_out, instr[25]);
  not not_51 (not_51_out, instr[26]);
  not not_52 (not_52_out, instr[27]);
  not not_53 (not_53_out, instr[28]);
  not not_54 (not_54_out, instr[29]);
  not not_55 (not_55_out, instr[31]);
  not not_56 (not_56_out, and_9_out);
  and and_9 (and_9_out, f3_2, f7_00);
  and hex0 (f3_0, not_26_out, not_27_out, not_28_out);
  and hex1 (f3_1, instr[12], not_29_out, not_30_out);
  and hex2 (f3_2, not_31_out, instr[13], not_32_out);
  and hex4 (f3_4, not_33_out, not_34_out, instr[14]);
  and hex5 (f3_5, instr[12], not_35_out, instr[14]);
  and hex6 (f3_6, not_36_out, instr[13], instr[14]);
  and hex7 (f3_7, instr[12], instr[13], instr[14]);
  and and_10 (f7_00, not_37_out, not_38_out, not_39_out, not_40_out, not_41_out, not_42_out, not_43_out);
  and and_11 (f7_01, instr[25], not_44_out, not_45_out, not_46_out, not_47_out, not_48_out, not_49_out);
  and and_12 (f7_20, not_50_out, not_51_out, not_52_out, not_53_out, not_54_out, instr[30], not_55_out);
  or or_3 (or_3_out, R, U, I_im);
  assign WBSel = I_load ? 2'b00 : 2'bz;  // Controlled_Buffer controlled_buffer_1
  assign WBSel = or_3_out ? 2'b01 : 2'bz;  // Controlled_Buffer controlled_buffer_2
  assign WBSel = or_4_out ? 2'b10 : 2'bz;  // Controlled_Buffer controlled_buffer_3
  or or_4 (or_4_out, I_jalr, J);
  and and_13 (and_13_out, and_14_out, R);
  and and_14 (and_14_out, f3_2, f7_00);
  and R_add (R_add_out, R, f3_0, f7_00);
  or or_5 (or_5_out, and_13_out, and_15_out);
  and and_15 (and_15_out, I_im, f3_2);
  and I_addi (I_addi_out, I_im, f3_0);
  or or_6 (or_6_out, R_and_out, I_andi_out);
  and I_andi (I_andi_out, I_im, f3_7);
  and R_and (R_and_out, f3_7, f7_00, R);
  or or_7 (or_7_out, R_add_out, I_load, I_addi_out, MemW, B, J, I_jalr);
  and R_or (R_or_out, f3_6, f7_00, R);
  assign MemLnth = and_16_out ? 2'b00 : 2'bz;  // Controlled_Buffer controlled_buffer_4
  and and_16 (and_16_out, I_load, f3_0);
  or or_8 (or_8_out, R_or_out, I_ori_out);
  and I_ori (I_ori_out, I_im, f3_6);
  and R_xor (R_xor_out, f3_4, f7_00, R);
  assign MemLnth = and_17_out ? 2'b01 : 2'bz;  // Controlled_Buffer controlled_buffer_5
  assign MemLnth = and_18_out ? 2'b10 : 2'bz;  // Controlled_Buffer controlled_buffer_6
  and and_17 (and_17_out, I_load, f3_1);
  assign ALUSel = or_7_out ? 4'b0000 : 4'bz;  // Controlled_Buffer controlled_buffer_7
  assign ALUSel = or_6_out ? 4'b0001 : 4'bz;  // Controlled_Buffer controlled_buffer_8
  or or_9 (or_9_out, R_xor_out, I_xori_out);
  and I_xori (I_xori_out, I_im, f3_4);
  and and_18 (and_18_out, I_load, f3_2);
  and and_19 (and_19_out, f3_5, f7_20);
  assign ALUSel = or_8_out ? 4'b0010 : 4'bz;  // Controlled_Buffer controlled_buffer_9
  assign ALUSel = or_9_out ? 4'b0011 : 4'bz;  // Controlled_Buffer controlled_buffer_10
  assign ALUSel = srl_srli_out ? 4'b0100 : 4'bz;  // Controlled_Buffer controlled_buffer_11
  assign ALUSel = sari_out ? 4'b0101 : 4'bz;  // Controlled_Buffer controlled_buffer_12
  and srl_srli (srl_srli_out, f3_5, f7_00);
  and and_20 (and_20_out, I_im, not_57_out);
  not not_57 (not_57_out, and_19_out);
  assign ALUSel = sll_slli_out ? 4'b0110 : 4'bz;  // Controlled_Buffer controlled_buffer_13
  assign ALUSel = slt_slti_out ? 4'b0111 : 4'bz;  // Controlled_Buffer controlled_buffer_14
  assign ALUSel = R_div_out ? 4'b1000 : 4'bz;  // Controlled_Buffer controlled_buffer_15
  assign ALUSel = R_rem_out ? 4'b1001 : 4'bz;  // Controlled_Buffer controlled_buffer_16
  and sari (sari_out, f3_5, f7_20);
  and and_21 (and_21_out, f3_5, f7_20);
  assign ImmSel = and_20_out ? 3'b000 : 3'bz;  // Controlled_Buffer controlled_buffer_17
  assign ImmSel = MemW ? 3'b001 : 3'bz;  // Controlled_Buffer controlled_buffer_18
  assign ImmSel = B ? 3'b010 : 3'bz;  // Controlled_Buffer controlled_buffer_19
  assign ImmSel = U ? 3'b011 : 3'bz;  // Controlled_Buffer controlled_buffer_20
  assign ALUSel = R_mult_out ? 4'b1010 : 4'bz;  // Controlled_Buffer controlled_buffer_21
  assign ALUSel = R_multh_out ? 4'b1011 : 4'bz;  // Controlled_Buffer controlled_buffer_22
  assign ALUSel = R_sub_out ? 4'b1100 : 4'bz;  // Controlled_Buffer controlled_buffer_23
  assign ALUSel = U ? 4'b1101 : 4'bz;  // Controlled_Buffer controlled_buffer_24
  and sll_slli (sll_slli_out, f3_1, or_10_out, f7_00);
  or or_10 (or_10_out, I_im, R);
  and and_22 (and_22_out, I_im, and_21_out);
  assign ImmSel = J ? 3'b100 : 3'bz;  // Controlled_Buffer controlled_buffer_25
  assign ImmSel = and_22_out ? 3'b101 : 3'bz;  // Controlled_Buffer controlled_buffer_26
  assign ImmSel = I_jalr ? 3'b110 : 3'bz;  // Controlled_Buffer controlled_buffer_27
  assign ImmSel = I_load ? 3'b111 : 3'bz;  // Controlled_Buffer controlled_buffer_28
  and R_div (R_div_out, R, f3_4, f7_01);
  and slt_slti (slt_slti_out, f3_2, or_11_out);
  or or_11 (or_11_out, I_im, R);
  and R_mult (R_mult_out, R, f3_0, f7_01);
  and R_rem (R_rem_out, R, f3_6, f7_01);
  and R_multh (R_multh_out, R, f3_1, f7_01);
  or or_12 (RegWEn, R, I_load, I_im, U, J, I_jalr);
  and R_sub (R_sub_out, R, f3_0, f7_20);
  or or_13 (ASel, B, J);
  not not_58 (BSel, R);
  and and_23 (BrUn, B, f3_6);

  // Other names for the same wires on the sheet: fun3[2:0] = instr[14:12]; i19_12[7:0] = instr[19:12];
  //   i31_12[19:0] = instr[31:12]; rs1[4:0] = instr[19:15]; i11_0[11:0] = instr[31:20]; i11_J = instr[20];
  //   rs2[4:0] = instr[24:20]; i10_1[9:0] = instr[30:21]; fun7[6:0] = instr[31:25]; i10_5[5:0] = instr[30:25];
  //   i11_5[6:0] = instr[31:25]; i12 = instr[31]; i20 = instr[31]; opcode[6:0] = instr[6:0]; i4_0[4:0] = instr[11:7];
  //   i11_B = instr[7]; rd[4:0] = instr[11:7]; i4_1[3:0] = instr[11:8]; S = MemW

  // Notes on the sheet:
  //   Inputs
  //   mem
  //   ALU
  //   pc+4
  //   Outputs
  //   load byte
  //   load half word
  //   load word
  //   add
  //   and
  //   or
  //   xor
  //   srl
  //   sra
  //   sll
  //   slt
  //   div
  //   rem
  //   mult
  //   multh
  //   sub
  //   bsel
  //   0: i_imm_except_srai
  //   1: s_imm
  //   2: b_imm
  //   3: u_imm
  //   4: j_imm
  //   5: i_imm_srai
  //   6: i_imm_jalr
endmodule

module ImmGen (
  input  [31:0] instr,
  input  [2:0] ImmSel,
  output [31:0] imm_32
);

  wire [31:0] bit_extender_1_out, bit_extender_2_out, bit_extender_3_out, bit_extender_4_out,
       bit_extender_5_out, bit_extender_6_out, bit_extender_7_out;

  assign bit_extender_1_out = {{19{instr[31]}}, {instr[31], instr[7], instr[30:25], instr[11:8], 1'b0}};  // Bit_Extender bit_extender_1
  assign bit_extender_2_out = {{20{instr[31]}}, {instr[31:25], instr[11:7]}};  // Bit_Extender bit_extender_2
  assign bit_extender_3_out = {{11{instr[31]}}, {instr[31], instr[19:12], instr[20], instr[30:21], 1'b0}};  // Bit_Extender bit_extender_3
  assign bit_extender_4_out = {{27{instr[24]}}, instr[24:20]};  // Bit_Extender bit_extender_4
  assign bit_extender_5_out = {{20{instr[31]}}, instr[31:20]};  // Bit_Extender bit_extender_5
  assign bit_extender_6_out = {{20{instr[31]}}, instr[31:20]};  // Bit_Extender bit_extender_6
  assign bit_extender_7_out = {{20{instr[31]}}, instr[31:20]};  // Bit_Extender bit_extender_7
  Multiplexer #(.select(3), .width(32), .enable("false")) multiplexer_1 (
    .in0(bit_extender_7_out), .in1(bit_extender_2_out), .in2(bit_extender_1_out),
    .in3({instr[31:12], {12{1'b0}}}), .in4(bit_extender_3_out), .in5(bit_extender_4_out),
    .in6(bit_extender_5_out), .in7(bit_extender_6_out), .out(imm_32), .sel(ImmSel));

  // Other names for the same wires on the sheet: i4_0[4:0] = instr[11:7]; i11_B = instr[7]; rd[4:0] = instr[11:7];
  //   i4_1[3:0] = instr[11:8]; fun3[2:0] = instr[14:12]; i19_12[7:0] = instr[19:12]; i31_12[19:0] = instr[31:12];
  //   rs1[4:0] = instr[19:15]; i11_0[11:0] = instr[31:20]; i11_J = instr[20]; rs2[4:0] = instr[24:20];
  //   i10_1[9:0] = instr[30:21]; fun7[6:0] = instr[31:25]; i10_5[5:0] = instr[30:25]; i11_5[6:0] = instr[31:25];
  //   i12 = instr[31]; i20 = instr[31]; opcode[6:0] = instr[6:0]

  // Notes on the sheet:
  //   Inputs
  //   2: b_imm
  //   1: s_imm
  //   4: j_imm
  //   0: i_imm_except_srai and load
  //   3: u_imm
  //   5: i_imm_srai
  //   6: i_jalr
  //   7: i_load
endmodule
