// Logisim project regfile.circ as structural Verilog: 3 circuits, main circuit main
module main (
  input  [4:0] Read_Register_1_rs1,
  input  [4:0] Read_Register_2_rs2,
  input  [4:0] Write_Register_rd,
  input  [31:0] Write_Data,
  input  Write_Enable,
  input  Clock,
  output [31:0] ra,
  output [31:0] sp,
  output [31:0] t0,
  output [31:0] t1,
  output [31:0] t2,
  output [31:0] s0,
  output [31:0] s1,
  output [31:0] a0,
  output [31:0] Read_Data_1,
  output [31:0] Read_Data_2
);

  regs regs_1 (
    .write_in(Write_Data), .clk(Clock), .w_en(Write_Enable), .w_reg(Write_Register_rd),
    .read1(Read_Register_1_rs1), .read2(Read_Register_2_rs2), .x1(ra), .x2(sp), .x5(t0), .x6(t1),
    .readout1(Read_Data_1), .x7(t2), .x8(s0), .readout2(Read_Data_2), .x9(s1), .x10(a0));

  // Other names for the same wires on the sheet: clk = Clock; read_data1[31:0] = Read_Data_1;
  //   read_data2[31:0] = Read_Data_2; read_reg1[4:0] = Read_Register_1_rs1; read_reg2[4:0] = Read_Register_2_rs2;
  //   write_en = Write_Enable; write_reg[4:0] = Write_Register_rd

  // Notes on the sheet:
  //   INPUTS to your circuit
  //   DON'T CHANGE THE LOCATIONS OF THE INPUTS AND OUTPUTS!
  //   These are DEBUG/TEST outputs from your circuit.
  //   OUTPUTS from your circuit
endmodule

// clock
module gated_reg (
  input  [31:0] intput_fccd64d3,
  input  write_enabe,
  input  clock,
  output [31:0] output_02ef1bc2
);

  Register #(.width(32)) register_1 (
    .D(intput_fccd64d3), .en(write_enabe), .clk(clock), .Q(output_02ef1bc2));  // open: clr
endmodule

module regs (
  input  [31:0] write_in,
  input  clk,
  input  w_en,
  input  [4:0] w_reg,
  input  [4:0] read1,
  input  [4:0] read2,
  output [31:0] x1,
  output [31:0] x2,
  output [31:0] x5,
  output [31:0] x6,
  output [31:0] readout1,
  output [31:0] x7,
  output [31:0] x8,
  output [31:0] readout2,
  output [31:0] x9,
  output [31:0] x10
);

  wire decoder_1_out0, decoder_1_out1, decoder_1_out2, decoder_1_out3, decoder_1_out4, decoder_1_out5,
       decoder_1_out6, decoder_1_out7, decoder_1_out8, decoder_1_out9, decoder_1_out10;
  wire [31:0] r3out, r4out, undriven, undriven_2;

  Multiplexer #(.select(5), .width(32), .enable("false")) multiplexer_1 (
    .in0({32{1'b0}}), .in1(x1), .in2(x2), .in3(undriven), .in4(undriven_2), .in5(x5), .in6(x6), .in7(x7),
    .in8(x8), .in9(x9), .in10(x10), .out(readout1), .sel(read1));  // open: in11, in12, in13, in14, in15, in16, in17, in18, in19, in20, in21, in22, in23, in24, in25, in26, in27, in28, in29, in30, in31
  Decoder #(.select(5)) decoder_1 (
    .out0(decoder_1_out0), .out1(decoder_1_out1), .out2(decoder_1_out2), .out3(decoder_1_out3),
    .out4(decoder_1_out4), .out5(decoder_1_out5), .out6(decoder_1_out6), .out7(decoder_1_out7),
    .out8(decoder_1_out8), .out9(decoder_1_out9), .out10(decoder_1_out10), .sel(w_reg), .en(w_en));  // open: out11, out12, out13, out14, out15, out16, out17, out18, out19, out20, out21, out22, out23, out24, out25, out26, out27, out28, out29, out30, out31
  // gated_reg reg4: pin names not known; wires that end beside it: clk, decoder_1_out4, write_in, r4out
  gated_reg reg10 (.output_02ef1bc2(x10), .clock(clk), .write_enabe(decoder_1_out10), .intput_fccd64d3(write_in));
  Multiplexer #(.select(5), .width(32), .enable("false")) multiplexer_2 (
    .in0({32{1'b0}}), .in1(x1), .in2(x2), .in3(undriven), .in4(undriven_2), .in5(x5), .in6(x6), .in7(x7),
    .in8(x8), .in9(x9), .in10(x10), .out(readout2), .sel(read2));  // open: in11, in12, in13, in14, in15, in16, in17, in18, in19, in20, in21, in22, in23, in24, in25, in26, in27, in28, in29, in30, in31
  gated_reg reg3 (.output_02ef1bc2(r3out));  // open: clock, write_enabe, intput_fccd64d3
  gated_reg reg9 (.output_02ef1bc2(x9), .clock(clk), .write_enabe(decoder_1_out9), .intput_fccd64d3(write_in));
  gated_reg reg2 (.output_02ef1bc2(x2), .clock(clk), .write_enabe(decoder_1_out2), .intput_fccd64d3(write_in));
  gated_reg reg8 (.output_02ef1bc2(x8), .clock(clk), .write_enabe(decoder_1_out8), .intput_fccd64d3(write_in));
  gated_reg reg1 (.output_02ef1bc2(x1), .clock(clk), .write_enabe(decoder_1_out1), .intput_fccd64d3(write_in));
  gated_reg reg7 (.output_02ef1bc2(x7), .clock(clk), .write_enabe(decoder_1_out7), .intput_fccd64d3(write_in));
  gated_reg reg6 (.output_02ef1bc2(x6), .clock(clk), .write_enabe(decoder_1_out6), .intput_fccd64d3(write_in));
  gated_reg reg5 (.output_02ef1bc2(x5), .clock(clk), .write_enabe(decoder_1_out5), .intput_fccd64d3(write_in));

  // Other names for the same wires on the sheet: r1out[31:0] = x1; r2out[31:0] = x2; r5out[31:0] = x5;
  //   r6out[31:0] = x6; r7out[31:0] = x7; r8out[31:0] = x8; r9out[31:0] = x9; r10out[31:0] = x10
endmodule
